// Logisim project Jean-Implementations.circ as structural Verilog
module Register_File (
  input  Clock,
  input  [4:0] Rs,
  input  [4:0] Rt,
  input  [4:0] Rd,
  input  [31:0] Write_Data,
  input  Reg_Write,
  input  Clear,
  output [31:0] Read_Data_1,
  output [31:0] Read_Data_2
);

  wire R0_Wreg, R1_Wreg, R2_Wreg, R3_Wreg, R4_Wreg, R5_Wreg, R6_Wreg, R7_Wreg, R8_Wreg, R9_Wreg, R10_Wreg,
       R11_Wreg, R12_Wreg, R13_Wreg, R14_Wreg, R15_Wreg, R16_Wreg, R17_Wreg, R18_Wreg, R19_Wreg, R20_Wreg,
       R21_Wreg, R22_Wreg, R23_Wreg, R24_Wreg, R25_Wreg, R26_Wreg, R27_Wreg, R28_Wreg, R29_Wreg, R30_Wreg,
       R31_Wreg;
  wire [31:0] R1, R2, R3, R4, R5, R6, R7, R8, R9, R10, R11, R12, R13, R14, R15, R16, R17, R18, R19, R20, R21,
       R22, R23, R24, R25, R26, R27, R28, R29, R30, R31;

  Multiplexer #(.select(5), .width(32)) multiplexer_1 (
    .in0({32{1'b0}}), .in1(R1), .in2(R2), .in3(R3), .in4(R4), .in5(R5), .in6(R6), .in7(R7), .in8(R8),
    .in9(R9), .in10(R10), .in11(R11), .in12(R12), .in13(R13), .in14(R14), .in15(R15), .in16(R16), .in17(R17),
    .in18(R18), .in19(R19), .in20(R20), .in21(R21), .in22(R22), .in23(R23), .in24(R24), .in25(R25),
    .in26(R26), .in27(R27), .in28(R28), .in29(R29), .in30(R30), .in31(R31), .out(Read_Data_1), .sel(Rs));  // open: en
  Multiplexer #(.select(5), .width(32)) multiplexer_2 (
    .in0({32{1'b0}}), .in1(R1), .in2(R2), .in3(R3), .in4(R4), .in5(R5), .in6(R6), .in7(R7), .in8(R8),
    .in9(R9), .in10(R10), .in11(R11), .in12(R12), .in13(R13), .in14(R14), .in15(R15), .in16(R16), .in17(R17),
    .in18(R18), .in19(R19), .in20(R20), .in21(R21), .in22(R22), .in23(R23), .in24(R24), .in25(R25),
    .in26(R26), .in27(R27), .in28(R28), .in29(R29), .in30(R30), .in31(R31), .out(Read_Data_2), .sel(Rt));  // open: en
  Decoder #(.select(5)) decoder_1 (
    .out0(R0_Wreg), .out1(R1_Wreg), .out2(R2_Wreg), .out3(R3_Wreg), .out4(R4_Wreg), .out5(R5_Wreg),
    .out6(R6_Wreg), .out7(R7_Wreg), .out8(R8_Wreg), .out9(R9_Wreg), .out10(R10_Wreg), .out11(R11_Wreg),
    .out12(R12_Wreg), .out13(R13_Wreg), .out14(R14_Wreg), .out15(R15_Wreg), .out16(R16_Wreg),
    .out17(R17_Wreg), .out18(R18_Wreg), .out19(R19_Wreg), .out20(R20_Wreg), .out21(R21_Wreg),
    .out22(R22_Wreg), .out23(R23_Wreg), .out24(R24_Wreg), .out25(R25_Wreg), .out26(R26_Wreg),
    .out27(R27_Wreg), .out28(R28_Wreg), .out29(R29_Wreg), .out30(R30_Wreg), .out31(R31_Wreg), .sel(Rd));  // open: en
  Register #(.width(32)) R (.D(Write_Data), .en(R1_Wreg), .Q(R1), .clk(Clock), .clr(Clear));
  Register #(.width(32)) R_2 (.D(Write_Data), .en(R2_Wreg), .Q(R2), .clk(Clock), .clr(Clear));
  Register #(.width(32)) R_3 (.D(Write_Data), .en(R3_Wreg), .Q(R3), .clk(Clock), .clr(Clear));
  Register #(.width(32)) R_4 (.D(Write_Data), .en(R4_Wreg), .Q(R4), .clk(Clock), .clr(Clear));
  Register #(.width(32)) R_5 (.D(Write_Data), .en(R5_Wreg), .Q(R5), .clk(Clock), .clr(Clear));
  Register #(.width(32)) R_6 (.D(Write_Data), .en(R6_Wreg), .Q(R6), .clk(Clock), .clr(Clear));
  Register #(.width(32)) R_7 (.D(Write_Data), .en(R7_Wreg), .Q(R7), .clk(Clock), .clr(Clear));
  Register #(.width(32)) R_8 (.D(Write_Data), .en(R8_Wreg), .Q(R8), .clk(Clock), .clr(Clear));
  Register #(.width(32)) R_9 (.D(Write_Data), .en(R9_Wreg), .Q(R9), .clk(Clock), .clr(Clear));
  Register #(.width(32)) R_10 (.D(Write_Data), .en(R10_Wreg), .Q(R10), .clk(Clock), .clr(Clear));
  Register #(.width(32)) R_11 (.D(Write_Data), .en(R11_Wreg), .Q(R11), .clk(Clock), .clr(Clear));
  Register #(.width(32)) R_12 (.D(Write_Data), .en(R12_Wreg), .Q(R12), .clk(Clock), .clr(Clear));
  Register #(.width(32)) R_13 (.D(Write_Data), .en(R13_Wreg), .Q(R13), .clk(Clock), .clr(Clear));
  Register #(.width(32)) R_14 (.D(Write_Data), .en(R14_Wreg), .Q(R14), .clk(Clock), .clr(Clear));
  Register #(.width(32)) R_15 (.D(Write_Data), .en(R15_Wreg), .Q(R15), .clk(Clock), .clr(Clear));
  Register #(.width(32)) R_16 (.D(Write_Data), .en(R16_Wreg), .Q(R16), .clk(Clock), .clr(Clear));
  Register #(.width(32)) R_17 (.D(Write_Data), .en(R17_Wreg), .Q(R17), .clk(Clock), .clr(Clear));
  Register #(.width(32)) R_18 (.D(Write_Data), .en(R18_Wreg), .Q(R18), .clk(Clock), .clr(Clear));
  Register #(.width(32)) R_19 (.D(Write_Data), .en(R19_Wreg), .Q(R19), .clk(Clock), .clr(Clear));
  Register #(.width(32)) R_20 (.D(Write_Data), .en(R20_Wreg), .Q(R20), .clk(Clock), .clr(Clear));
  Register #(.width(32)) R_21 (.D(Write_Data), .en(R21_Wreg), .Q(R21), .clk(Clock), .clr(Clear));
  Register #(.width(32)) R_22 (.D(Write_Data), .en(R23_Wreg), .Q(R22), .clk(Clock), .clr(Clear));
  Register #(.width(32)) R_23 (.D(Write_Data), .en(R23_Wreg), .Q(R23), .clk(Clock), .clr(Clear));
  Register #(.width(32)) R_24 (.D(Write_Data), .en(R24_Wreg), .Q(R24), .clk(Clock), .clr(Clear));
  Register #(.width(32)) R_25 (.D(Write_Data), .en(R25_Wreg), .Q(R25), .clk(Clock), .clr(Clear));
  Register #(.width(32)) R_26 (.D(Write_Data), .en(R26_Wreg), .Q(R26), .clk(Clock), .clr(Clear));
  Register #(.width(32)) R_27 (.D(Write_Data), .en(R27_Wreg), .Q(R27), .clk(Clock), .clr(Clear));
  Register #(.width(32)) R_28 (.D(Write_Data), .en(R28_Wreg), .Q(R28), .clk(Clock), .clr(Clear));
  Register #(.width(32)) R_29 (.D(Write_Data), .en(R29_Wreg), .Q(R29), .clk(Clock), .clr(Clear));
  Register #(.width(32)) R_30 (.D(Write_Data), .en(R30_Wreg), .Q(R30), .clk(Clock), .clr(Clear));
  Register #(.width(32)) R_31 (.D(Write_Data), .en(R31_Wreg), .Q(R31), .clk(Clock), .clr(Clear));

  // Other names for the same wires on the sheet: CLK = Clock; WData[31:0] = Write_Data; WReg = Reg_Write

  // Notes on the sheet:
  //   Registers
endmodule

module Instruction_Decoder (
  input  [31:0] Instruction,
  output halt,
  output nop,
  output tty,
  output rnd,
  output kbd,
  output mfhi,
  output mflo,
  output j,
  output jr,
  output be,
  output bgtz,
  output blez,
  output bne,
  output bltz,
  output pop,
  output push,
  output lw,
  output sw,
  output [3:0] alu_operador,
  output logic_i,
  output [4:0] Rs,
  output [4:0] Rt,
  output [27:0] destino,
  output mul_div,
  output [4:0] Rd,
  output [31:0] constante_3,
  output [31:0] constante,
  output [31:0] constante_2,
  output RF_zero,
  output pop_push,
  output lw_sw,
  output inmediate,
  output load_zero,
  output load_Rd,
  output [1:0] data_to_RF
);

  wire a, add, add_i, ai, \and , and_7_out, and_8_out, and_9_out, and_10_out, and_11_out, and_46_out,
       and_47_out, and_i, branch, div, div_u, func_code____0, func_code____1, func_code____011, mul, mul_u,
       \nor , op_code____0, op_code____1, opp_aritmetica, \or , or_3_out, or_9_out, or_10_out, or_11_out,
       or_12_out, or_13_out, or_14_out, or_15_out, or_i, slt, slt_i, slt_u, sltu_i, sub, \xor , xor_i;

  or or_1 (logic_i, and_i, or_i, xor_i);
  and and_1 (func_code____1, Instruction[0], Instruction[1], Instruction[2], Instruction[3], Instruction[4], Instruction[5]);
  and and_2 (func_code____0, ~Instruction[0], ~Instruction[1], ~Instruction[2], ~Instruction[3], ~Instruction[4], ~Instruction[5]);  // AND_Gate
  and and_3 (op_code____1, Instruction[26], Instruction[27], Instruction[28], Instruction[29], Instruction[30], Instruction[31]);
  and and_4 (op_code____0, ~Instruction[26], ~Instruction[27], ~Instruction[28], ~Instruction[29], ~Instruction[30], ~Instruction[31]);  // AND_Gate
  and and_5 (branch, ~Instruction[29], ~Instruction[30], ~Instruction[31], ~op_code____0);  // AND_Gate
  and and_6 (pop_push, ~Instruction[26], ~Instruction[27], ~Instruction[28], Instruction[29], Instruction[30], Instruction[31]);  // AND_Gate
  and and_7 (and_7_out, Instruction[29], ~Instruction[30], ~Instruction[31]);  // AND_Gate
  and and_8 (and_8_out, op_code____0, ~nop, ~mfhi, ~mflo, ~jr, ~func_code____011);  // AND_Gate
  and and_9 (and_9_out, Instruction[29], ~Instruction[30], ~Instruction[31]);  // AND_Gate
  or or_2 (RF_zero, blez, bgtz, bltz);
  and and_10 (and_10_out, opp_aritmetica, ~inmediate);  // AND_Gate
  and and_11 (and_11_out, ~load_Rd, ~inmediate);  // AND_Gate
  Priority_Encoder #(.select(2)) priority_encoder_1 (
    .in0(1'b1), .in1(mfhi), .in2(mflo), .in3(or_3_out), .out(data_to_RF));  // open: gs, en_out, en_in
  or or_3 (or_3_out, pop, lw);
  or or_4 (opp_aritmetica, and_7_out, and_8_out);
  or or_5 (inmediate, and_9_out, lw, sw);
  or or_6 (load_Rd, and_10_out, rnd, mflo, pop, mfhi, kbd);
  or or_7 (load_zero, and_11_out, sw);
  and and_12 (func_code____011, Instruction[3], Instruction[4], ~Instruction[5]);  // AND_Gate
  or or_8 (lw_sw, lw, sw);
  and and_13 (halt, op_code____1, func_code____1);
  and and_14 (nop, op_code____0, func_code____0);
  and and_15 (mfhi, op_code____0, ~Instruction[0], ~Instruction[1], ~Instruction[2], ~Instruction[3], Instruction[4], ~Instruction[5]);  // AND_Gate
  and and_16 (mflo, op_code____0, ~Instruction[0], Instruction[1], ~Instruction[2], ~Instruction[3], Instruction[4], ~Instruction[5]);  // AND_Gate
  and and_17 (be, ~Instruction[26], ~Instruction[27], Instruction[28], branch);  // AND_Gate
  and and_18 (bne, Instruction[26], ~Instruction[27], Instruction[28], branch);  // AND_Gate
  and and_19 (blez, ~Instruction[26], Instruction[27], Instruction[28], branch);  // AND_Gate
  Repetidor repetidor_1 (.Signal(1'b0), ._16(constante_3[31:16]));  // open: _14
  and and_20 (tty, op_code____1, ~halt, Instruction[0]);  // AND_Gate
  and and_21 (rnd, op_code____1, ~halt, Instruction[1]);  // AND_Gate
  and and_22 (kbd, op_code____1, ~halt, Instruction[2]);  // AND_Gate
  and and_23 (j, ~Instruction[26], Instruction[27], ~Instruction[28], ~Instruction[29], ~Instruction[30], ~Instruction[31]);  // AND_Gate
  and and_24 (jr, op_code____0, ~Instruction[0], ~Instruction[1], ~Instruction[2], Instruction[3], ~Instruction[4], ~Instruction[5]);  // AND_Gate
  and and_25 (bgtz, Instruction[26], Instruction[27], Instruction[28], branch);
  and and_26 (bltz, Instruction[26], ~Instruction[27], ~Instruction[28], branch);  // AND_Gate
  and and_27 (pop, pop_push, func_code____0);
  and and_28 (add_i, ~Instruction[26], ~Instruction[27], ~Instruction[28], ai);  // AND_Gate
  and and_29 (slt_i, ~Instruction[26], Instruction[27], ~Instruction[28], ai);  // AND_Gate
  and and_30 (sltu_i, Instruction[26], Instruction[27], ~Instruction[28], ai);  // AND_Gate
  Repetidor repetidor_2 (.Signal(Instruction[15]), ._16(constante[31:16]), ._14(constante_2[31:18]));
  and and_31 (lw, Instruction[26], Instruction[27], ~Instruction[28], ~Instruction[29], ~Instruction[30], Instruction[31]);  // AND_Gate
  and and_32 (ai, opp_aritmetica, inmediate);
  and and_33 (push, pop_push, Instruction[0], ~Instruction[1], ~Instruction[2], ~Instruction[3], ~Instruction[4], ~Instruction[5]);  // AND_Gate
  and and_34 (sw, Instruction[26], Instruction[27], ~Instruction[28], Instruction[29], ~Instruction[30], Instruction[31]);  // AND_Gate
  and and_35 (and_i, ~Instruction[26], ~Instruction[27], Instruction[28], ai);  // AND_Gate
  and and_36 (or_i, Instruction[26], ~Instruction[27], Instruction[28], ai);  // AND_Gate
  and and_37 (xor_i, ~Instruction[26], Instruction[27], Instruction[28], ai);  // AND_Gate
  and and_38 (add, a, ~Instruction[0], ~Instruction[1], ~Instruction[2], ~Instruction[3], ~Instruction[4], Instruction[5]);  // AND_Gate
  and and_39 (sub, a, ~Instruction[0], Instruction[1], ~Instruction[2], ~Instruction[3], ~Instruction[4], Instruction[5]);  // AND_Gate
  and and_40 (mul, a, ~Instruction[0], ~Instruction[1], ~Instruction[2], Instruction[3], Instruction[4], ~Instruction[5]);  // AND_Gate
  and and_41 (mul_u, a, Instruction[0], ~Instruction[1], ~Instruction[2], Instruction[3], Instruction[4], ~Instruction[5]);  // AND_Gate
  or or_9 (or_9_out, add, add_i, lw_sw);
  or or_10 (or_10_out, branch, sub);
  or or_11 (or_11_out, slt, slt_i);
  or or_12 (or_12_out, slt_u, sltu_i);
  or or_13 (or_13_out, \and , and_i);
  or or_14 (or_14_out, \or , or_i);
  or or_15 (or_15_out, \xor , xor_i);
  and and_42 (div, a, ~Instruction[0], Instruction[1], ~Instruction[2], Instruction[3], Instruction[4], ~Instruction[5]);  // AND_Gate
  and and_43 (div_u, a, Instruction[0], Instruction[1], ~Instruction[2], Instruction[3], Instruction[4], ~Instruction[5]);  // AND_Gate
  and and_44 (slt, a, ~Instruction[0], Instruction[1], ~Instruction[2], Instruction[3], ~Instruction[4], Instruction[5]);  // AND_Gate
  and and_45 (slt_u, a, Instruction[0], Instruction[1], ~Instruction[2], Instruction[3], ~Instruction[4], Instruction[5]);  // AND_Gate
  Priority_Encoder #(.select(4)) priority_encoder_2 (
    .in0(or_9_out), .in1(or_10_out), .in2(mul), .in3(mul_u), .in4(div), .in5(div_u), .in6(or_11_out),
    .in7(or_12_out), .in8(or_13_out), .in9(or_14_out), .in10(\nor ), .in11(or_15_out), .out(alu_operador));  // open: in12, in13, in14, in15, gs, en_out, en_in
  and and_46 (and_46_out, op_code____0, func_code____011);
  or or_16 (a, and_46_out, and_47_out);
  and and_47 (and_47_out, opp_aritmetica, op_code____0);
  or or_17 (mul_div, mul, mul_u, div, div_u);
  and and_48 (\and , a, ~Instruction[0], ~Instruction[1], Instruction[2], ~Instruction[3], ~Instruction[4], Instruction[5]);  // AND_Gate
  and and_49 (\or , a, Instruction[0], ~Instruction[1], Instruction[2], ~Instruction[3], ~Instruction[4], Instruction[5]);  // AND_Gate
  and and_50 (\nor , a, Instruction[0], Instruction[1], Instruction[2], ~Instruction[3], ~Instruction[4], Instruction[5]);  // AND_Gate
  and and_51 (\xor , a, ~Instruction[0], ~Instruction[1], ~Instruction[2], Instruction[3], ~Instruction[4], Instruction[5]);  // AND_Gate

  assign constante[15:0] = Instruction[15:0];
  assign constante_2[17:0] = {Instruction[15:0], 2'b00};
  assign constante_3[15:0] = Instruction[15:0];
  assign destino = {Instruction[25:0], 2'b00};
  assign Rd = Instruction[15:11];
  assign Rs = Instruction[25:21];
  assign Rt = Instruction[20:16];

  // Other names for the same wires on the sheet: constante_t[15:0] = Instruction[15:0];
  //   destino_t[25:0] = Instruction[25:0]; func_code[5:0] = Instruction[5:0]; op_code[5:0] = Instruction[31:26]

  // Notes on the sheet:
  //   Decodificar
  //   General
  //   mfhi && mflo
  //   Branch
  //   jump
  //   pop/push
  //   load/store word
  //   Inmediate
  //   Aritmetica
endmodule

module Datapath (
  input  [31:0] Data,
  input  clr_I,
  input  en,
  input  Pop_load,
  input  exc_I_2,
  input  Push_load,
  input  load_I,
  input  clk,
  input  exc_I,
  input  clr,
  input  [6:0] kbd_data,
  input  kbd_aviable
);

  wire [31:0] bit_extender_1_out, kbd_data_t;

  assign bit_extender_1_out = {{25{1'b0}}, kbd_data};  // Bit_Extender bit_extender_1
  Multiplexer #(.width(32), .enable("false")) multiplexer_1 (
    .in0({32{1'b1}}), .in1(bit_extender_1_out), .out(kbd_data_t), .sel(kbd_aviable));
  Instruction_Decoder instruction_decoder_1 ();  // open: Instruction, constante_3, constante, constante_2, halt, nop, tty, rnd, kbd, mfhi, mflo, j, jr, be, bgtz, blez, bne, bltz, pop, push, lw, sw, alu_operador, logic_i, Rs, Rt, destino, mul_div, Rd, RF_zero, pop_push, lw_sw, inmediate, load_zero, load_Rd, data_to_RF
endmodule

module Repetidor (
  input  Signal,
  output [15:0] _16,
  output [13:0] _14
);


  assign _14 = {14{Signal}};
  assign _16 = {16{Signal}};
endmodule
