// Logisim project Ray-Implementations.circ as structural Verilog
module ALU (
  input  [3:0] S,
  input  [31:0] A,
  input  [31:0] B,
  output [31:0] R,
  output [31:0] hi,
  output zero,
  output [31:0] lo,
  output neg
);

  wire comparator_2_lt, comparator_3_lt, EN;
  wire [31:0] ADD, AND, DIVS_HI, DIVS_LO, DIVU_HI, DIVU_LO, MULT_HI, MULT_LO, MULU_HI, MULU_LO, NOR, OR, SLT,
       SLTU, SUB, XOR;

  // Probe on A
  // Probe on B
  // Probe on lo
  Comparator #(.width(32)) comparator_1 (.a(lo), .b({32{1'b0}}), .eq(zero), .lt(neg));  // open: gt
  Adder #(.width(32)) adder_1 (.a(A), .b(B), .out(ADD));  // open: cin, cout
  Subtractor #(.width(32)) subtractor_1 (.a(A), .b(B), .out(SUB));  // open: bin, bout
  Multiplier #(.width(32)) multiplier_1 (.a(A), .b(B), .out(MULU_LO), .cout(MULU_HI));  // open: cin
  Divider #(.width(32)) divider_1 (.a(A), .b(B), .out(DIVU_LO), .rem(DIVU_HI));  // open: upper
  DivS DIVS (.A(A), .B(B), .LowOutput(DIVS_LO), .HighOutput(DIVS_HI));
  Multiplexer #(.select(2), .width(32)) multiplexer_1 (
    .in0(MULT_HI), .in1(MULU_HI), .in2(DIVS_HI), .in3(DIVU_HI), .out(hi), .sel(S[1:0]), .en(EN));
  nor nor_1 (EN, S[2], S[3]);
  assign OR = A | B;  // OR_Gate or_1, 32 bits wide
  assign AND = A & B;  // AND_Gate and_1, 32 bits wide
  assign NOR = ~(A | B);  // NOR_Gate nor_2, 32 bits wide
  assign XOR = A ^ B;  // XOR_Gate xor_1, 32 bits wide
  Comparator #(.width(32)) comparator_2 (.a(A), .b(B), .lt(comparator_2_lt));  // open: gt, eq
  Comparator #(.width(32), .mode("unsigned")) comparator_3 (.a(A), .b(B), .lt(comparator_3_lt));  // open: gt, eq
  Multiplexer #(.width(32), .enable("false")) multiplexer_2 (
    .in0({32{1'b0}}), .in1(32'h1), .out(SLT), .sel(comparator_2_lt));
  Multiplexer #(.width(32), .enable("false")) multiplexer_3 (
    .in0({32{1'b0}}), .in1(32'h1), .out(SLTU), .sel(comparator_3_lt));
  Multiplexer #(.select(4), .width(32), .enable("false")) multiplexer_4 (
    .in0(ADD), .in1(SUB), .in2(MULT_LO), .in3(MULU_LO), .in4(DIVS_LO), .in5(DIVU_LO), .in6(SLT), .in7(SLTU),
    .in8(AND), .in9(OR), .in10(NOR), .in11(XOR), .out(lo), .sel(S));  // open: in12, in13, in14, in15

  assign R = lo;

  // Other names for the same wires on the sheet: RESULT[31:0] = lo; HL[1:0] = S[1:0]; SELECT[3:0] = S

  // Notes on the sheet:
  //   DIVU
  //   ARITMÉTICA
  //   MULU
  //   LÓGICA
  //   COMPARACIÓN
  //   revisar division y agregar smult
  //   revisar signo
endmodule

module DivS (
  input  [31:0] A,
  input  [31:0] B,
  output [31:0] LowOutput,
  output [31:0] HighOutput
);

  wire xor_1_out;
  wire [31:0] divider_1_out, multiplexer_1_out, multiplexer_2_out, negator_1_out, negator_2_out,
       negator_3_out;

  Negator #(.width(32)) negator_1 (.in(A), .out(negator_1_out));
  Negator #(.width(32)) negator_2 (.in(B), .out(negator_2_out));
  Multiplexer #(.width(32), .enable("false")) multiplexer_1 (
    .in0(A), .in1(negator_1_out), .out(multiplexer_1_out), .sel(A[31]));
  Multiplexer #(.width(32), .enable("false")) multiplexer_2 (
    .in0(B), .in1(negator_2_out), .out(multiplexer_2_out), .sel(B[31]));
  Divider #(.width(32)) divider_1 (
    .a(multiplexer_1_out), .b(multiplexer_2_out), .out(divider_1_out), .rem(HighOutput));  // open: upper
  Negator #(.width(32)) negator_3 (.in(divider_1_out), .out(negator_3_out));
  xor xor_1 (xor_1_out, A[31], B[31]);
  // Probe on LowOutput
  Multiplexer #(.width(32), .enable("false")) multiplexer_3 (
    .in0(divider_1_out), .in1(negator_3_out), .out(LowOutput), .sel(xor_1_out));
  // Probe on HighOutput

  // Notes on the sheet:
  //   SIGNED DIV
endmodule

module prueba (
  input  [3:0] in_1,
  input  [3:0] in_2,
  input  [3:0] in_3,
  input  [3:0] in_4,
  output [3:0] out_5,
  output [3:0] out_6
);

  // Probe on in_1
  // Probe on in_3
  // Probe on out_5
  Multiplier #(.width(4)) multiplier_1 (.a(in_1), .b(in_3), .out(out_5));  // open: cin, cout
  // Probe on in_2
  // Probe on in_4
  // Probe on out_6
  Divider #(.width(4)) divider_1 (.a(in_2), .b(in_4), .out(out_6));  // open: upper, rem
endmodule
